# Fritzing sketch 02 - 9V Battery Powers LED with Breadboard (saved by Fritzing 0.9.3b)
breadboards: 1

parts:
  BAT1 = BC9VPC [package=bc9vpc]
  LED1 = LED - 5mm [color="Red (633nm)" package="5 mm [THT]"]
  R1 = Resistor [tolerance=±5% resistance=220 package="1206 [SMD]"]

nets:
  N1: BAT1.V+, R1.Pin_1
  N2: BAT1.V-, LED1.cathode
  N3: LED1.anode, R1.Pin_0
