# Fritzing sketch 05 - LED and programmable pad (saved by Fritzing 0.9.3b)
breadboards: 1

parts:
  LED1 = LED - 5mm [color="Red (633nm)" package="5 mm [THT]"]
  Part1 = Adafruit Circuit Playground Express [part_number="Adafruit #3333"]

nets:
  N1: LED1.cathode, Part1.GND
  N2: LED1.anode, Part1.D12_A0_SPEAKER

custom parts:
  Adafruit Circuit Playground Express: Circuit Playground Express is the next step towards a perfect introduction to electronics and programming. We've taken the original Circuit Playground Classic and made it even better! Not only did we pack even more sensors in, we also made it even easier to program. You can now start your journey with Microsoft MakeCode block-based or Javascript programming. Then, you can use the same board to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
