# Fritzing sketch 06 - Continuous servo (saved by Fritzing 0.9.3b)
breadboards: 1

parts:
  J1 = Basic Servo
  Part2 = Adafruit Circuit Playground Express [part_number="Adafruit #3333"]
  HC-SR04_Sensor_2 = HC-SR04 Ultrasonic Distance Sensor

nets:
  GND: J1.gnd, Part2.GND, HC-SR04_Sensor_2.GND
  VCC: J1.vcc, Part2.VOUT, HC-SR04_Sensor_2.VCC
  N1: J1.pulse, Part2.D6_A1
  N2: Part2.D9_A2, HC-SR04_Sensor_2.ECHO
  N3: Part2.D10_A3, HC-SR04_Sensor_2.TRIG

custom parts:
  Adafruit Circuit Playground Express: Circuit Playground Express is the next step towards a perfect introduction to electronics and programming. We've taken the original Circuit Playground Classic and made it even better! Not only did we pack even more sensors in, we also made it even easier to program. You can now start your journey with Microsoft MakeCode block-based or Javascript programming. Then, you can use the same board to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
