# Fritzing sketch 09 - Proximity Detector w Servo (saved by Fritzing 0.9.3b)
breadboards: 1

parts:
  Part1 = Adafruit Circuit Playground Express [part_number="Adafruit #3333"]
  HC-SR04_Sensor_1 = HC-SR04 Ultrasonic Distance Sensor
  J2 = Basic Servo

nets:
  N1: Part1.D6_A1, HC-SR04_Sensor_1.TRIG
  GND: Part1.GND, HC-SR04_Sensor_1.GND, J2.gnd
  N2: Part1.D9_A2, HC-SR04_Sensor_1.ECHO
  N3: Part1.D1_A7_TX, J2.pulse
  VCC: Part1.VOUT, HC-SR04_Sensor_1.VCC, J2.vcc

custom parts:
  Adafruit Circuit Playground Express: Circuit Playground Express is the next step towards a perfect introduction to electronics and programming. We've taken the original Circuit Playground Classic and made it even better! Not only did we pack even more sensors in, we also made it even easier to program. You can now start your journey with Microsoft MakeCode block-based or Javascript programming. Then, you can use the same board to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
