# Fritzing sketch 06 - Continuous servo (saved by Fritzing 0.9.3b)

parts:
  Part1 = Adafruit Circuit Playground Express [part_number="Adafruit #3333"]
  J1 = Basic Servo

nets:
  N1: Part1.D6_A1, J1.pulse
  GND: Part1.GND, J1.gnd
  N2: Part1.VOUT, J1.vcc

custom parts:
  Adafruit Circuit Playground Express: Circuit Playground Express is the next step towards a perfect introduction to electronics and programming. We've taken the original Circuit Playground Classic and made it even better! Not only did we pack even more sensors in, we also made it even easier to program. You can now start your journey with Microsoft MakeCode block-based or Javascript programming. Then, you can use the same board to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
